# Fritzing sketch Entwurf-V2 (saved by Fritzing 0.9.4)
circuit board: 4.46771cm x 3.85461cm

parts:
  S1 = Pushbutton [package="[THT]"]
  R1 = Resistor [tolerance=±5% resistance=220 package=THT]
  R2 = Resistor [tolerance=±5% resistance=220 package=THT]
  LED3 = LED - 5mm [color="Red (633nm)" package="5 mm [THT]"]
  LED2 = LED - 5mm [color="Green (560nm)" package="5 mm [THT]"]
  WeMos_D1_Mini2 = WeMos D1 Mini
  WeMos_D1_Mini_Protoboard_Shield1 = WeMos D1 Mini Protoboard Shield

nets:
  N1: S1.Pin_1, S1.Pin_2, R1.Pin_1, R2.Pin_1, WeMos_D1_Mini2.G, WeMos_D1_Mini_Protoboard_Shield1.X3-Y1, WeMos_D1_Mini_Protoboard_Shield1.X4-Y8, WeMos_D1_Mini_Protoboard_Shield1.X5-Y9, WeMos_D1_Mini_Protoboard_Shield1.X6-Y1
  N2: S1.Pin_3, S1.Pin_4, LED3.cathode, LED2.cathode, WeMos_D1_Mini2.D1, WeMos_D1_Mini_Protoboard_Shield1.D1, WeMos_D1_Mini_Protoboard_Shield1.G, WeMos_D1_Mini_Protoboard_Shield1.X3-Y3, WeMos_D1_Mini_Protoboard_Shield1.X3-Y10, WeMos_D1_Mini_Protoboard_Shield1.X6-Y3, WeMos_D1_Mini_Protoboard_Shield1.X6-Y10, WeMos_D1_Mini_Protoboard_Shield1.X6-Y11, WeMos_D1_Mini_Protoboard_Shield1.X7-Y3, WeMos_D1_Mini_Protoboard_Shield1.X7-Y7
  N3: R1.Pin_0, WeMos_D1_Mini_Protoboard_Shield1.D2, WeMos_D1_Mini_Protoboard_Shield1.X4-Y4, WeMos_D1_Mini_Protoboard_Shield1.X7-Y4
  N4: R2.Pin_0, WeMos_D1_Mini_Protoboard_Shield1.D3, WeMos_D1_Mini_Protoboard_Shield1.X5-Y5, WeMos_D1_Mini_Protoboard_Shield1.X7-Y5
  N5: LED3.anode, WeMos_D1_Mini_Protoboard_Shield1.X4-Y10
  N6: LED2.anode, WeMos_D1_Mini_Protoboard_Shield1.X5-Y10
