# Fritzing sketch Entwurf (saved by Fritzing 0.9.4)
circuit board: 4.46771cm x 3.85461cm
breadboards: 1

parts:
  WeMos_D1_Mini2 = WeMos D1 Mini
  S1 = Pushbutton [package="[THT]"]
  R1 = Resistor [tolerance=±5% resistance=220 package=THT]
  R2 = Resistor [tolerance=±5% resistance=220 package=THT]
  LED3 = LED - 5mm [color="Red (633nm)" package="5 mm [THT]"]
  LED2 = LED - 5mm [color="Green (560nm)" package="5 mm [THT]"]

nets:
  N1: WeMos_D1_Mini2.D1, S1.Pin_3, S1.Pin_4
  N2: WeMos_D1_Mini2.D2, LED3.anode
  N3: WeMos_D1_Mini2.D3, LED2.anode
  N4: WeMos_D1_Mini2.G, S1.Pin_1, S1.Pin_2, R1.Pin_1, R2.Pin_1
  N5: R1.Pin_0, LED3.cathode
  N6: R2.Pin_0, LED2.cathode
